# Fritzing sketch sketch- fritzing (saved by Fritzing 0.9.4)
breadboards: 1

parts:
  U1 = NodeMCU V3.0
  U2 = LCD-16X2 [package=lcd-16x2]  # not connected
  Chirp!_Soil_Moisture_Sensor1 = Chirp! Soil Moisture Sensor v2.7.3
  ESP32_-_Back1 = ESP32 - CAM
  Part1 = Arduino Ethernet Shield (Rev3)
  DS1 = DS18B20 1-Wire Temperature Sensor Probe Cable
  WATER_PUMP1 = water pump/motor
  KY-1 = Keyes Relay [package=THT]
  Mod1 = KY-015 Temperature & Humidity Sensor Module [package="Breakout board"]
  R1 = Resistor [tolerance=±5% resistance=220 package="2010 [SMD]"]

nets:
  N1: U1.D3, KY-1.ground
  N2: U1.3V3, KY-1.signal, KY-1.C
  N3: U1.GND#6, U1.GND#13, U1.GND#16, U1.GND#33, Chirp!_Soil_Moisture_Sensor1.pin_5, DS1.GND, WATER_PUMP1.pin_1, KY-1.power, Mod1.-
  N4: U1.D5, DS1.shield, R1.Pin_0
  N5: U1.D7, Mod1.Vin
  N6: U1.RX, ESP32_-_Back1.GPIO3_/_RX
  N7: U1.TX, ESP32_-_Back1.GPIO1_/_TX
  VIN: U1.Vin, Chirp!_Soil_Moisture_Sensor1.Pin_1, DS1.VDD, Mod1.S, R1.Pin_1
  N8: U1.A0, Chirp!_Soil_Moisture_Sensor1.pin_3
  GND: ESP32_-_Back1.GND, Part1.GND
  5V: ESP32_-_Back1.5V, Part1.5V
  N9: WATER_PUMP1.pin_2, KY-1.NO

custom parts:
  NodeMCU V3.0: ESP8266 based NodeMCU
  ESP32 - CAM: The ESP32-CAM has a very competitive small-size camera module that can operate independently as a minimum system with a footprint of only 27*40.5*4.5mm and a deep sleep current of up to 6mA.
  water pump/motor: WATER PUMP BY ARDUBLOCKTR
  Keyes Relay: The Keyes 5V relay module is suitable for SCM development, home appliance control. It uses a 5V~12V TIL control signal which can control DC / AC signal.
  KY-015 Temperature & Humidity Sensor Module: KY-015 temperature and humidity sensor module, provides a low-latency serial interface to measure humidity and temperature.
